// Logisim project CRC.circ as structural Verilog: 2 circuits, main circuit 4bit xor
module _4bit_xor (
  input  [3:0] in_1,
  input  [3:0] in_2,
  output [2:0] out_3,
  output out_4
);

  wire [3:0] xor_1_out;
  wire [3:3] multiplexer_1_out;

  assign xor_1_out = in_1 ^ in_2;  // XOR_Gate xor_1, 4 bits wide
  Multiplexer #(.width(4)) multiplexer_1 (
    .in0(in_1), .in1(xor_1_out), .out({multiplexer_1_out[3], out_3}), .sel(in_1[3]));  // open: en

  assign out_4 = in_1[3];

  // Other names for the same wires on the sheet: select = in_1[3]
endmodule

module CRC (
  input  [7:0] in_1,
  input  [3:0] in_2,
  output [10:0] out_3
);

  wire [2:0] n4bit_xor_1_out_3, n4bit_xor_2_out_3, n4bit_xor_3_out_3, n4bit_xor_4_out_3, n4bit_xor_5_out_3,
       n4bit_xor_7_out_3;
  wire [3:1] n4bit_xor_6_out_3;

  _4bit_xor u_4bit_xor_1 (.in_1(in_1[7:4]), .in_2(in_2), .out_3(n4bit_xor_1_out_3));  // open: out_4
  _4bit_xor u_4bit_xor_2 (.in_1({n4bit_xor_1_out_3, in_1[3]}), .in_2(in_2), .out_3(n4bit_xor_2_out_3));  // open: out_4
  _4bit_xor u_4bit_xor_3 (.in_1({n4bit_xor_2_out_3, in_1[2]}), .in_2(in_2), .out_3(n4bit_xor_3_out_3));  // open: out_4
  _4bit_xor u_4bit_xor_4 (.in_1({n4bit_xor_3_out_3, in_1[1]}), .in_2(in_2), .out_3(n4bit_xor_4_out_3));  // open: out_4
  _4bit_xor u_4bit_xor_5 (.in_1({n4bit_xor_4_out_3, in_1[0]}), .in_2(in_2), .out_3(n4bit_xor_5_out_3));  // open: out_4
  _4bit_xor u_4bit_xor_6 (.in_1({n4bit_xor_5_out_3, 1'b0}), .in_2(in_2), .out_3(n4bit_xor_6_out_3));  // open: out_4
  _4bit_xor u_4bit_xor_7 (.in_1({n4bit_xor_6_out_3, 1'b0}), .in_2(in_2), .out_3(n4bit_xor_7_out_3));  // open: out_4
  _4bit_xor u_4bit_xor_8 (.in_1({n4bit_xor_7_out_3, 1'b0}), .in_2(in_2), .out_3(out_3[2:0]));  // open: out_4

  assign out_3[10:3] = in_1;

  // Other names for the same wires on the sheet: chushu[3:0] = in_2; bit0 = in_1[0]; bit1 = in_1[1]; bit2 = in_1[2];
  //   bit3 = in_1[3]; beichu1[3:0] = in_1[7:4]
endmodule
