// Logisim project ftoijsh.circ as structural Verilog: 1 circuit, main circuit ftoi
module ftoi (
  input  [15:0] in_1,
  output [31:0] out_2
);

  wire comparator_1_eq, comparator_2_eq, comparator_3_gt;
  wire [4:0] subtractor_1_out, subtractor_2_out;
  wire [31:0] multiplexer_1_out, multiplexer_2_out, negator_1_out, \nor , shifter_1_out, shifter_2_out;

  Negator #(.width(32)) negator_1 (.in(\nor ), .out(negator_1_out));
  Multiplexer #(.width(32)) multiplexer_1 (
    .in0(\nor ), .in1(negator_1_out), .out(multiplexer_1_out), .sel(in_1[15]));  // open: en
  Subtractor #(.width(5)) subtractor_1 (.a(5'b11001), .b(in_1[14:10]), .out(subtractor_1_out));  // open: bin, bout
  Subtractor #(.width(5)) subtractor_2 (.a(in_1[14:10]), .b(5'b11001), .out(subtractor_2_out));  // open: bin, bout
  Comparator #(.width(5), .mode("unsigned")) comparator_1 (
    .a(in_1[14:10]), .b({5{1'b0}}), .eq(comparator_1_eq));  // open: gt, lt
  // Probe on subtractor_1_out
  Multiplexer #(.width(32)) multiplexer_2 (
    .in0(multiplexer_1_out), .in1({32{1'b0}}), .out(multiplexer_2_out), .sel(comparator_1_eq));  // open: en
  Shifter #(.width(32), .shift("lr")) shifter_1 (
    .in({22'h1, in_1[9:0]}), .\dist (subtractor_1_out), .out(shifter_1_out));
  Shifter #(.width(32)) shifter_2 (.in({22'h1, in_1[9:0]}), .\dist (subtractor_2_out), .out(shifter_2_out));
  Comparator #(.width(5), .mode("unsigned")) comparator_2 (
    .a({5{1'b1}}), .b(in_1[14:10]), .eq(comparator_2_eq));  // open: gt, lt
  Comparator #(.width(5), .mode("unsigned")) comparator_3 (
    .a(in_1[14:10]), .b(5'b11000), .gt(comparator_3_gt));  // open: eq, lt
  Multiplexer #(.width(32)) multiplexer_3 (
    .in0(shifter_1_out), .in1(shifter_2_out), .out(\nor ), .sel(comparator_3_gt));  // open: en
  Multiplexer #(.width(32)) multiplexer_4 (
    .in0(multiplexer_2_out), .in1({32{1'b0}}), .out(out_2), .sel(comparator_2_eq));  // open: en

  // Other names for the same wires on the sheet: F[9:0] = in_1[9:0]; E[4:0] = in_1[14:10]; S = in_1[15]
endmodule
