// Logisim project main.circ as structural Verilog: 1 circuit, main circuit grf
module grf (
  input  [4:0] in_1,
  input  in_2,
  input  in_3,
  input  [4:0] in_4,
  input  [4:0] in_5,
  input  [31:0] in_6,
  input  in_7,
  output [31:0] out_8,
  output [31:0] out_9
);

  wire [31:0] R0, R1, R2, R3, R4, R5, R6, R7, R8, R9, R10, R11, R12, R13, R14, R15, R16, R17, R18, R19, R20,
       R21, R22, R23, R24, R25, R26, R27, R28, R29, R30, R31, W0, W1, W2, W3, W4, W5, W6, W7, W8, W9, W10,
       W11, W12, W13, W14, W15, W16, W17, W18, W19, W20, W21, W22, W23, W24, W25, W26, W27, W28, W29, W30,
       W31;

  Register #(.width(32)) register_1 (.D(W0), .en(in_3), .Q(R0), .clk(in_2), .clr(in_7));
  Register #(.width(32)) register_2 (.D(W4), .en(in_3), .Q(R4), .clk(in_2), .clr(in_7));
  Register #(.width(32)) register_3 (.D(W8), .en(in_3), .Q(R8), .clk(in_2), .clr(in_7));
  Register #(.width(32)) register_4 (.D(W12), .en(in_3), .Q(R12), .clk(in_2), .clr(in_7));
  Register #(.width(32)) register_5 (.D(W16), .en(in_3), .Q(R16), .clk(in_2), .clr(in_7));
  Register #(.width(32)) register_6 (.D(W20), .en(in_3), .Q(R20), .clk(in_2), .clr(in_7));
  Register #(.width(32)) register_7 (.D(W24), .en(in_3), .Q(R24), .clk(in_2), .clr(in_7));
  Register #(.width(32)) register_8 (.D(W28), .en(in_3), .Q(R28), .clk(in_2), .clr(in_7));
  Register #(.width(32)) register_9 (.D(W1), .en(in_3), .Q(R1), .clk(in_2), .clr(in_7));
  Register #(.width(32)) register_10 (.D(W5), .en(in_3), .Q(R5), .clk(in_2), .clr(in_7));
  Register #(.width(32)) register_11 (.D(W9), .en(in_3), .Q(R9), .clk(in_2), .clr(in_7));
  Register #(.width(32)) register_12 (.D(W13), .en(in_3), .Q(R13), .clk(in_2), .clr(in_7));
  Register #(.width(32)) register_13 (.D(W17), .en(in_3), .Q(R17), .clk(in_2), .clr(in_7));
  Register #(.width(32)) register_14 (.D(W21), .en(in_3), .Q(R21), .clk(in_2), .clr(in_7));
  Register #(.width(32)) register_15 (.D(W25), .en(in_3), .Q(R25), .clk(in_2), .clr(in_7));
  Register #(.width(32)) register_16 (.D(W29), .en(in_3), .Q(R29), .clk(in_2), .clr(in_7));
  Register #(.width(32)) register_17 (.D(W2), .en(in_3), .Q(R2), .clk(in_2), .clr(in_7));
  Register #(.width(32)) register_18 (.D(W6), .en(in_3), .Q(R6), .clk(in_2), .clr(in_7));
  Register #(.width(32)) register_19 (.D(W10), .en(in_3), .Q(R10), .clk(in_2), .clr(in_7));
  Register #(.width(32)) register_20 (.D(W14), .en(in_3), .Q(R14), .clk(in_2), .clr(in_7));
  Register #(.width(32)) register_21 (.D(W18), .en(in_3), .Q(R18), .clk(in_2), .clr(in_7));
  Register #(.width(32)) register_22 (.D(W22), .en(in_3), .Q(R22), .clk(in_2), .clr(in_7));
  Register #(.width(32)) register_23 (.D(W26), .en(in_3), .Q(R26), .clk(in_2), .clr(in_7));
  Register #(.width(32)) register_24 (.D(W30), .en(in_3), .Q(R30), .clk(in_2), .clr(in_7));
  Register #(.width(32)) register_25 (.D(W3), .en(in_3), .Q(R3), .clk(in_2), .clr(in_7));
  Register #(.width(32)) register_26 (.D(W7), .en(in_3), .Q(R7), .clk(in_2), .clr(in_7));
  Register #(.width(32)) register_27 (.D(W11), .en(in_3), .Q(R11), .clk(in_2), .clr(in_7));
  Register #(.width(32)) register_28 (.D(W15), .en(in_3), .Q(R15), .clk(in_2), .clr(in_7));
  Register #(.width(32)) register_29 (.D(W19), .en(in_3), .Q(R19), .clk(in_2), .clr(in_7));
  Register #(.width(32)) register_30 (.D(W23), .en(in_3), .Q(R23), .clk(in_2), .clr(in_7));
  Register #(.width(32)) register_31 (.D(W27), .en(in_3), .Q(R27), .clk(in_2), .clr(in_7));
  Register #(.width(32)) register_32 (.D(W31), .en(in_3), .Q(R31), .clk(in_2), .clr(in_7));
  Multiplexer #(.select(5), .width(32)) multiplexer_1 (
    .in0({32{1'b0}}), .in1(R1), .in2(R2), .in3(R3), .in4(R4), .in5(R5), .in6(R6), .in7(R7), .in8(R8),
    .in9(R9), .in10(R10), .in11(R11), .in12(R12), .in13(R13), .in14(R14), .in15(R15), .in16(R16), .in17(R17),
    .in18(R18), .in19(R19), .in20(R20), .in21(R21), .in22(R22), .in23(R23), .in24(R24), .in25(R25),
    .in26(R26), .in27(R27), .in28(R28), .in29(R29), .in30(R30), .in31(R31), .out(out_9), .sel(in_4));  // open: en
  Multiplexer #(.select(5), .width(32)) multiplexer_2 (
    .in0({32{1'b0}}), .in1(R1), .in2(R2), .in3(R3), .in4(R4), .in5(R5), .in6(R6), .in7(R7), .in8(R8),
    .in9(R9), .in10(R10), .in11(R11), .in12(R12), .in13(R13), .in14(R14), .in15(R15), .in16(R16), .in17(R17),
    .in18(R18), .in19(R19), .in20(R20), .in21(R21), .in22(R22), .in23(R23), .in24(R24), .in25(R25),
    .in26(R26), .in27(R27), .in28(R28), .in29(R29), .in30(R30), .in31(R31), .out(out_8), .sel(in_1));  // open: en
  Demultiplexer #(.select(5), .width(32), .tristate("true")) demultiplexer_1 (
    .out0(W0), .out1(W1), .out2(W2), .out3(W3), .out4(W4), .out5(W5), .out6(W6), .out7(W7), .out8(W8),
    .out9(W9), .out10(W10), .out11(W11), .out12(W12), .out13(W13), .out14(W14), .out15(W15), .out16(W16),
    .out17(W17), .out18(W18), .out19(W19), .out20(W20), .out21(W21), .out22(W22), .out23(W23), .out24(W24),
    .out25(W25), .out26(W26), .out27(W27), .out28(W28), .out29(W29), .out30(W30), .out31(W31), .in(in_6),
    .sel(in_5));  // open: en

  // Other names for the same wires on the sheet: A1[4:0] = in_1; A2[4:0] = in_4; A3[4:0] = in_5; clk = in_2;
  //   en = in_3; reset = in_7; WD[31:0] = in_6
endmodule
