// Logisim project navigationjsh.circ as structural Verilog: 3 circuits, main circuit navigation
module navigation (
  input  [1:0] in_1,
  input  in_2,
  input  in_3,
  output arrive,
  output hit
);

  wire \hit输出逻辑_hit , not_1_out, not_2_out;
  wire [2:0] register_1_q, \次态逻辑_ns0 ;

  \次态逻辑  \u_次态逻辑  (
    .s2(register_1_q[2]), .s1(register_1_q[1]), .s0(register_1_q[0]), .d1(in_1[1]), .d0(in_1[0]),
    .ns2(\次态逻辑_ns0 [2]), .ns1(\次态逻辑_ns0 [1]), .ns0(\次态逻辑_ns0 [0]));
  Register #(.width(3)) register_1 (.D(\次态逻辑_ns0 ), .Q(register_1_q), .clk(in_2), .clr(in_3));  // open: en
  not not_1 (not_1_out, register_1_q[1]);
  and and_1 (arrive, register_1_q[2], not_1_out, not_2_out);
  not not_2 (not_2_out, register_1_q[0]);
  \hit输出逻辑  \hit输出逻辑  (
    .s2(register_1_q[2]), .s1(register_1_q[1]), .s0(register_1_q[0]), .d1(in_1[1]), .d0(in_1[0]),
    .hit(\hit输出逻辑_hit ));
  Register #(.width(1)) register_2 (.D(\hit输出逻辑_hit ), .Q(hit), .clk(in_2), .clr(in_3));  // open: en

  // Notes on the sheet:
  //   下一状态
  //   当前状态
endmodule

module \次态逻辑  (
  input  s2,
  input  s1,
  input  s0,
  input  d1,
  input  d0,
  output ns2,
  output ns1,
  output ns0
);

  wire and_1_out, and_2_out, and_3_out, and_4_out, and_5_out, and_6_out, and_7_out, and_8_out, and_9_out,
       and_10_out, and_11_out, not_1_out, not_2_out, not_3_out, not_4_out, not_5_out, not_6_out, not_7_out,
       not_8_out, not_9_out, not_10_out, not_11_out, not_12_out, not_13_out, not_14_out, not_15_out,
       not_16_out, not_17_out;

  not not_1 (not_1_out, s0);
  not not_2 (not_2_out, d1);
  not not_3 (not_3_out, d0);
  not not_4 (not_4_out, d1);
  not not_5 (not_5_out, s1);
  not not_6 (not_6_out, d1);
  not not_7 (not_7_out, d1);
  not not_8 (not_8_out, d0);
  not not_9 (not_9_out, s0);
  not not_10 (not_10_out, d1);
  not not_11 (not_11_out, s0);
  not not_12 (not_12_out, d0);
  not not_13 (not_13_out, s2);
  not not_14 (not_14_out, s1);
  not not_15 (not_15_out, d1);
  not not_16 (not_16_out, d0);
  not not_17 (not_17_out, d0);
  and and_1 (and_1_out, s1, not_1_out, not_2_out, not_3_out);
  and and_2 (and_2_out, s1, s0, not_4_out, d0);
  and and_3 (and_3_out, not_5_out, s0, not_6_out);
  and and_4 (and_4_out, s0, not_7_out, not_8_out);
  and and_5 (and_5_out, s1, not_9_out, not_10_out, d0);
  and and_6 (and_6_out, s1, not_11_out, d1, not_12_out);
  and and_7 (and_7_out, s1, s0, d1, d0);
  and and_8 (and_8_out, not_13_out, not_14_out, not_15_out, not_16_out);
  and and_9 (and_9_out, s0, d1, d0);
  and and_10 (and_10_out, s1, d1, d0);
  and and_11 (and_11_out, s1, s0, not_17_out);
  or or_1 (ns2, and_1_out, and_2_out);
  or or_2 (ns1, and_3_out, and_4_out, and_5_out, and_6_out, and_7_out);
  or or_3 (ns0, and_8_out, and_9_out, and_10_out, and_11_out);
endmodule

module \hit输出逻辑  (
  input  s2,
  input  s1,
  input  s0,
  input  d1,
  input  d0,
  output hit
);

  wire and_1_out, and_2_out, and_3_out, and_4_out, and_5_out, not_1_out, not_2_out, not_3_out, not_4_out,
       not_5_out, not_6_out, not_7_out, not_8_out, not_9_out, not_10_out, not_11_out;

  not not_1 (not_1_out, s2);
  not not_2 (not_2_out, s0);
  not not_3 (not_3_out, d1);
  not not_4 (not_4_out, s2);
  not not_5 (not_5_out, s1);
  not not_6 (not_6_out, s0);
  not not_7 (not_7_out, s2);
  not not_8 (not_8_out, s0);
  not not_9 (not_9_out, d0);
  not not_10 (not_10_out, d1);
  not not_11 (not_11_out, d0);
  and and_1 (and_1_out, not_1_out, not_2_out, not_3_out, d0);
  and and_2 (and_2_out, not_4_out, not_5_out, not_6_out, d1);
  and and_3 (and_3_out, not_7_out, not_8_out, d1, not_9_out);
  and and_4 (and_4_out, s0, d1, d0);
  and and_5 (and_5_out, s1, s0, not_10_out, not_11_out);
  or or_1 (hit, and_1_out, and_2_out, and_3_out, and_4_out, and_5_out);
endmodule
