// Logisim project CPUimpsll.circ as structural Verilog: 15 circuits, main circuit grf
module grf (
  input  [4:0] in_1,
  input  in_2,
  input  in_3,
  input  [4:0] in_4,
  input  [4:0] in_5,
  input  [31:0] in_6,
  input  in_7,
  output [31:0] out_8,
  output [31:0] out_9
);

  wire [31:0] R0, R1, R2, R3, R4, R5, R6, R7, R8, R9, R10, R11, R12, R13, R14, R15, R16, R17, R18, R19, R20,
       R21, R22, R23, R24, R25, R26, R27, R28, R29, R30, R31, W0, W1, W2, W3, W4, W5, W6, W7, W8, W9, W10,
       W11, W12, W13, W14, W15, W16, W17, W18, W19, W20, W21, W22, W23, W24, W25, W26, W27, W28, W29, W30,
       W31;

  Register #(.width(32)) register_1 (.D(W0), .en(in_3), .Q(R0), .clk(in_2), .clr(in_7));
  Register #(.width(32)) register_2 (.D(W4), .en(in_3), .Q(R4), .clk(in_2), .clr(in_7));
  Register #(.width(32)) register_3 (.D(W8), .en(in_3), .Q(R8), .clk(in_2), .clr(in_7));
  Register #(.width(32)) register_4 (.D(W12), .en(in_3), .Q(R12), .clk(in_2), .clr(in_7));
  Register #(.width(32)) register_5 (.D(W16), .en(in_3), .Q(R16), .clk(in_2), .clr(in_7));
  Register #(.width(32)) register_6 (.D(W20), .en(in_3), .Q(R20), .clk(in_2), .clr(in_7));
  Register #(.width(32)) register_7 (.D(W24), .en(in_3), .Q(R24), .clk(in_2), .clr(in_7));
  Register #(.width(32)) register_8 (.D(W28), .en(in_3), .Q(R28), .clk(in_2), .clr(in_7));
  Register #(.width(32)) register_9 (.D(W1), .en(in_3), .Q(R1), .clk(in_2), .clr(in_7));
  Register #(.width(32)) register_10 (.D(W5), .en(in_3), .Q(R5), .clk(in_2), .clr(in_7));
  Register #(.width(32)) register_11 (.D(W9), .en(in_3), .Q(R9), .clk(in_2), .clr(in_7));
  Register #(.width(32)) register_12 (.D(W13), .en(in_3), .Q(R13), .clk(in_2), .clr(in_7));
  Register #(.width(32)) register_13 (.D(W17), .en(in_3), .Q(R17), .clk(in_2), .clr(in_7));
  Register #(.width(32)) register_14 (.D(W21), .en(in_3), .Q(R21), .clk(in_2), .clr(in_7));
  Register #(.width(32)) register_15 (.D(W25), .en(in_3), .Q(R25), .clk(in_2), .clr(in_7));
  Register #(.width(32)) register_16 (.D(W29), .en(in_3), .Q(R29), .clk(in_2), .clr(in_7));
  Register #(.width(32)) register_17 (.D(W2), .en(in_3), .Q(R2), .clk(in_2), .clr(in_7));
  Register #(.width(32)) register_18 (.D(W6), .en(in_3), .Q(R6), .clk(in_2), .clr(in_7));
  Register #(.width(32)) register_19 (.D(W10), .en(in_3), .Q(R10), .clk(in_2), .clr(in_7));
  Register #(.width(32)) register_20 (.D(W14), .en(in_3), .Q(R14), .clk(in_2), .clr(in_7));
  Register #(.width(32)) register_21 (.D(W18), .en(in_3), .Q(R18), .clk(in_2), .clr(in_7));
  Register #(.width(32)) register_22 (.D(W22), .en(in_3), .Q(R22), .clk(in_2), .clr(in_7));
  Register #(.width(32)) register_23 (.D(W26), .en(in_3), .Q(R26), .clk(in_2), .clr(in_7));
  Register #(.width(32)) register_24 (.D(W30), .en(in_3), .Q(R30), .clk(in_2), .clr(in_7));
  Register #(.width(32)) register_25 (.D(W3), .en(in_3), .Q(R3), .clk(in_2), .clr(in_7));
  Register #(.width(32)) register_26 (.D(W7), .en(in_3), .Q(R7), .clk(in_2), .clr(in_7));
  Register #(.width(32)) register_27 (.D(W11), .en(in_3), .Q(R11), .clk(in_2), .clr(in_7));
  Register #(.width(32)) register_28 (.D(W15), .en(in_3), .Q(R15), .clk(in_2), .clr(in_7));
  Register #(.width(32)) register_29 (.D(W19), .en(in_3), .Q(R19), .clk(in_2), .clr(in_7));
  Register #(.width(32)) register_30 (.D(W23), .en(in_3), .Q(R23), .clk(in_2), .clr(in_7));
  Register #(.width(32)) register_31 (.D(W27), .en(in_3), .Q(R27), .clk(in_2), .clr(in_7));
  Register #(.width(32)) register_32 (.D(W31), .en(in_3), .Q(R31), .clk(in_2), .clr(in_7));
  Multiplexer #(.select(5), .width(32)) multiplexer_1 (
    .in0({32{1'b0}}), .in1(R1), .in2(R2), .in3(R3), .in4(R4), .in5(R5), .in6(R6), .in7(R7), .in8(R8),
    .in9(R9), .in10(R10), .in11(R11), .in12(R12), .in13(R13), .in14(R14), .in15(R15), .in16(R16), .in17(R17),
    .in18(R18), .in19(R19), .in20(R20), .in21(R21), .in22(R22), .in23(R23), .in24(R24), .in25(R25),
    .in26(R26), .in27(R27), .in28(R28), .in29(R29), .in30(R30), .in31(R31), .out(out_9), .sel(in_4));  // open: en
  Multiplexer #(.select(5), .width(32)) multiplexer_2 (
    .in0({32{1'b0}}), .in1(R1), .in2(R2), .in3(R3), .in4(R4), .in5(R5), .in6(R6), .in7(R7), .in8(R8),
    .in9(R9), .in10(R10), .in11(R11), .in12(R12), .in13(R13), .in14(R14), .in15(R15), .in16(R16), .in17(R17),
    .in18(R18), .in19(R19), .in20(R20), .in21(R21), .in22(R22), .in23(R23), .in24(R24), .in25(R25),
    .in26(R26), .in27(R27), .in28(R28), .in29(R29), .in30(R30), .in31(R31), .out(out_8), .sel(in_1));  // open: en
  Demultiplexer #(.select(5), .width(32), .tristate("true")) demultiplexer_1 (
    .out0(W0), .out1(W1), .out2(W2), .out3(W3), .out4(W4), .out5(W5), .out6(W6), .out7(W7), .out8(W8),
    .out9(W9), .out10(W10), .out11(W11), .out12(W12), .out13(W13), .out14(W14), .out15(W15), .out16(W16),
    .out17(W17), .out18(W18), .out19(W19), .out20(W20), .out21(W21), .out22(W22), .out23(W23), .out24(W24),
    .out25(W25), .out26(W26), .out27(W27), .out28(W28), .out29(W29), .out30(W30), .out31(W31), .in(in_6),
    .sel(in_5));  // open: en

  // Other names for the same wires on the sheet: A1[4:0] = in_1; A2[4:0] = in_4; A3[4:0] = in_5; clk = in_2;
  //   en = in_3; reset = in_7; WD[31:0] = in_6
endmodule

module main (
  input  in_1,
  output [31:0] out_2,
  output out_3,
  output [4:0] out_4,
  output [31:0] out_5,
  output out_6,
  output [4:0] out_7,
  output [31:0] out_8
);

  wire alu_1_out_4, ALUSrc, clock_1_out, clock_2_out, clock_3_out, jump, MemtoReg, PcSrc, sll_con,
       \主译码器_1_branch , \主译码器_1_regdst ;
  wire [1:0] alu_1_out_5, \主译码器_1_out_12 ;
  wire [2:0] \主译码器_1_out_6 ;
  wire [4:0] S, \分线器_1_out_3 , \分线器_1_out_4 , \分线器_1_out_5 ;
  wire [5:0] func, OP;
  wire [15:0] imme;
  wire [24:0] alu_1_out_5_2;
  wire [25:0] \分线器_1_out_8 ;
  wire [31:0] adder_1_out, adder_2_out, bit_extender_1_out, dm_1_out_6, extender_1_out_4, grf_1_out_8,
       jpc_1_out_3, multiplexer_1_out, multiplexer_2_out, multiplexer_5_out, multiplexer_6_out, register_1_q,
       shifter_1_out, \sll扩展板_1_out_3 ;

  Multiplexer #(.width(32)) multiplexer_1 (
    .in0(adder_1_out), .in1(adder_2_out), .out(multiplexer_1_out), .sel(PcSrc));  // open: en
  Multiplexer #(.width(32)) multiplexer_2 (
    .in0(multiplexer_1_out), .in1(jpc_1_out_3), .out(multiplexer_2_out), .sel(jump));  // open: en
  Clock clock_1 (.out(clock_1_out));
  Register #(.width(32)) register_1 (
    .D(multiplexer_2_out), .Q(register_1_q), .clk(clock_1_out), .clr(in_1));  // open: en
  IM im_1 (.in_1(register_1_q), .out_2(out_2));
  Adder #(.width(32)) adder_1 (.a(register_1_q), .b(32'h4), .out(adder_1_out));  // open: cin, cout
  \分线器  \u_分线器_1  (
    .in_1(out_2), .out_2(OP), .out_3(\分线器_1_out_3 ), .out_4(\分线器_1_out_4 ), .out_5(\分线器_1_out_5 ),
    .out_6(func), .out_7(imme), .out_8(\分线器_1_out_8 ), .out_9(S));
  JPC jpc_1 (.out_3(jpc_1_out_3), .in_2(\分线器_1_out_8 ), .in_1(register_1_q));
  \主译码器  \u_主译码器_1  (
    .in_1(OP), .in_2(func), .MemtoReg(MemtoReg), .Memwrite(out_6), .branch(\主译码器_1_branch ),
    .out_6(\主译码器_1_out_6 ), .ALUSrc(ALUSrc), .RegDst(\主译码器_1_regdst ), .RegWrite(out_3), .JUMP(jump),
    .out_12(\主译码器_1_out_12 ));  // open: out_11
  Multiplexer #(.width(5)) multiplexer_3 (
    .in0(\分线器_1_out_4 ), .in1(\分线器_1_out_5 ), .out(out_4), .sel(\主译码器_1_regdst ));  // open: en
  Clock clock_2 (.out(clock_2_out));
  Multiplexer #(.width(32)) multiplexer_4 (
    .in0(multiplexer_6_out), .in1(\sll扩展板_1_out_3 ), .out(out_5), .sel(sll_con));  // open: en
  grf grf_1 (
    .in_1(\分线器_1_out_3 ), .in_4(\分线器_1_out_4 ), .in_5(out_4), .in_6(out_5), .out_8(grf_1_out_8),
    .out_9(out_8), .in_2(clock_2_out), .in_3(out_3), .in_7(in_1));
  assign bit_extender_1_out = {{16{imme[15]}}, imme};  // Bit_Extender bit_extender_1
  \sll扩展板  \sll扩展板_1  (.out_3(\sll扩展板_1_out_3 ), .in_1(multiplexer_6_out), .in_2(S));
  Multiplexer #(.width(32)) multiplexer_5 (
    .in0(out_8), .in1(bit_extender_1_out), .out(multiplexer_5_out), .sel(ALUSrc));  // open: en
  extender extender_1 (.in_3(multiplexer_5_out), .in_2(imme), .in_1(\主译码器_1_out_12 ), .out_4(extender_1_out_4));
  Shifter #(.width(32)) shifter_1 (.in(bit_extender_1_out), .\dist (5'b00010), .out(shifter_1_out));
  ALU alu_1 (
    .in_2(grf_1_out_8), .in_3(extender_1_out_4), .out_4(alu_1_out_4),
    .out_5({alu_1_out_5_2, out_7, alu_1_out_5}), .in_1(\主译码器_1_out_6 ));
  Adder #(.width(32)) adder_2 (.a(shifter_1_out), .b(adder_1_out), .out(adder_2_out));  // open: cin, cout
  and and_1 (PcSrc, \主译码器_1_branch , alu_1_out_4);
  Clock clock_3 (.out(clock_3_out));
  DM dm_1 (
    .in_3({alu_1_out_5_2, out_7, alu_1_out_5}), .in_4(out_8), .out_6(dm_1_out_6), .in_1(clock_3_out),
    .in_5(in_1), .in_2(out_6));
  Multiplexer #(.width(32)) multiplexer_6 (
    .in0({alu_1_out_5_2, out_7, alu_1_out_5}), .in1(dm_1_out_6), .out(multiplexer_6_out), .sel(MemtoReg));  // open: en

  // Other names for the same wires on the sheet: MemAddr[4:0] = out_7; instr[31:0] = out_2; MemData[31:0] = out_8;
  //   MemWrite = out_6; RegAddr[4:0] = out_4; RegData[31:0] = out_5; RegWrite = out_3; reset = in_1

  // Notes on the sheet:
  //   IM
  //   RegDst
endmodule

module IM (
  input  [31:0] in_1,
  output [31:0] out_2
);

  ROM #(.addrWidth(5), .dataWidth(32)) rom_1 (.addr(in_1[6:2]), .data(out_2));  // open: sel
endmodule

module \分线器  (
  input  [31:0] in_1,
  output [5:0] out_2,
  output [4:0] out_3,
  output [4:0] out_4,
  output [4:0] out_5,
  output [5:0] out_6,
  output [15:0] out_7,
  output [25:0] out_8,
  output [4:0] out_9
);


  assign out_2 = in_1[31:26];
  assign out_3 = in_1[25:21];
  assign out_4 = in_1[20:16];
  assign out_5 = in_1[15:11];
  assign out_6 = in_1[5:0];
  assign out_7 = in_1[15:0];
  assign out_8 = in_1[25:0];
  assign out_9 = in_1[10:6];
endmodule

module ALU (
  input  [2:0] in_1,
  input  [31:0] in_2,
  input  [31:0] in_3,
  output out_4,
  output [31:0] out_5
);

  wire comparator_1_eq;
  wire [31:0] adder_1_out, and_1_out, bit_extender_1_out, or_1_out, subtractor_1_out, xor_1_out;

  assign and_1_out = in_2 & in_3;  // AND_Gate and_1, 32 bits wide
  assign or_1_out = in_2 | in_3;  // OR_Gate or_1, 32 bits wide
  Adder #(.width(32)) adder_1 (.a(in_2), .b(in_3), .out(adder_1_out));  // open: cin, cout
  Subtractor #(.width(32)) subtractor_1 (.a(in_2), .b(in_3), .out(subtractor_1_out));  // open: bin, bout
  assign xor_1_out = in_2 ^ in_3;  // XOR_Gate xor_1, 32 bits wide
  Comparator #(.width(32), .mode("unsigned")) comparator_1 (.a(in_2), .b(in_3), .eq(comparator_1_eq));  // open: gt, lt
  assign bit_extender_1_out = {{31{1'b0}}, comparator_1_eq};  // Bit_Extender bit_extender_1
  Multiplexer #(.select(3), .width(32)) multiplexer_1 (
    .in0(and_1_out), .in1(or_1_out), .in2(adder_1_out), .in3(subtractor_1_out), .in4(xor_1_out),
    .in5(bit_extender_1_out), .out(out_5), .sel(in_1));  // open: in6, in7, en
  Comparator #(.width(32), .mode("unsigned")) comparator_2 (.a(out_5), .b({32{1'b0}}), .eq(out_4));  // open: gt, lt

  // Other names for the same wires on the sheet: dataA[31:0] = in_2; dataB[31:0] = in_3; select[2:0] = in_1
endmodule

module DM (
  input  in_1,
  input  in_2,
  input  [31:0] in_3,
  input  [31:0] in_4,
  input  in_5,
  output [31:0] out_6
);

  RAM #(.addrWidth(5), .dataWidth(32), .bus("separate")) ram_1 (
    .addr(in_3[6:2]), .din(in_4), .data(out_6), .str(in_2), .clk(in_1), .clr(in_5));  // open: sel, ld

  // Other names for the same wires on the sheet: clk = in_1; write = in_2
endmodule

module JPC (
  input  [31:0] in_1,
  input  [25:0] in_2,
  output [31:0] out_3
);


  assign out_3 = {in_1[31:28], in_2, 2'b00};
endmodule

module \主译码器  (
  input  [5:0] in_1,
  input  [5:0] in_2,
  output MemtoReg,
  output Memwrite,
  output branch,
  output [2:0] out_6,
  output ALUSrc,
  output RegDst,
  output RegWrite,
  output JUMP,
  output out_11,
  output [1:0] out_12
);

  wire liu_out, not_1_out, not_2_out, not_3_out, not_4_out, not_5_out, not_6_out, ori_out, R_out,
       special_1_out_2, special_1_out_3;
  wire [2:0] ALUop0_out;

  not not_1 (not_1_out, in_1[5]);
  not not_2 (not_2_out, in_1[3]);
  not not_3 (not_3_out, in_1[4]);
  not not_4 (not_4_out, in_1[1]);
  not not_5 (not_5_out, in_1[2]);
  special special_1 (.in_1(in_2), .out_2(special_1_out_2), .out_3(special_1_out_3));
  not not_6 (not_6_out, in_1[0]);
  and R (R_out, not_1_out, not_3_out, not_2_out, special_1_out_3, not_5_out, not_4_out, not_6_out);
  and LW (MemtoReg, in_1[5], not_3_out, not_2_out, not_5_out, in_1[1], in_1[0]);
  and SW (Memwrite, in_1[5], not_3_out, in_1[3], not_5_out, in_1[1], in_1[0]);
  and beq (branch, not_1_out, not_3_out, not_2_out, in_1[2], not_4_out, not_6_out);
  and J (JUMP, not_1_out, not_3_out, not_2_out, not_5_out, in_1[1], not_6_out);
  and ori (ori_out, not_1_out, not_3_out, in_1[3], in_1[2], not_4_out, in_1[0]);
  and liu (liu_out, not_1_out, not_3_out, in_1[3], in_1[2], in_1[1], in_1[0]);
  and sll (out_11, not_1_out, not_3_out, not_2_out, not_5_out, not_4_out, not_6_out, special_1_out_2);
  or or_1 (ALUSrc, Memwrite, MemtoReg);
  or or_2 (RegWrite, R_out, ori_out, out_11, liu_out, MemtoReg);
  or or_3 (RegDst, R_out, out_11);
  or ALUop2 (ALUop0_out[2], liu_out, out_11);
  or ALUop1 (ALUop0_out[1], R_out, ori_out);
  or ALUop0 (ALUop0_out[0], branch, ori_out);
  buf ext1 (out_12[1], liu_out);  // OR_Gate
  buf ext0 (out_12[0], ori_out);  // OR_Gate
  \ALU译码器  \alu译码器_1  (.in_1(ALUop0_out), .in_2(in_2), .out_3(out_6));

  // Other names for the same wires on the sheet: ALUctr[2:0] = out_6; func[5:0] = in_2
endmodule

module \ALU译码器  (
  input  [2:0] in_1,
  input  [5:0] in_2,
  output [2:0] out_3
);

  wire addu_out, beq_out, Lui_sll_out, lw_sw_out, not_1_out, not_2_out, not_3_out, not_4_out, not_5_out,
       not_6_out, not_7_out, not_8_out, not_9_out, ori_out, subu_out;

  not not_1 (not_1_out, in_2[4]);
  not not_2 (not_2_out, in_2[5]);
  not not_3 (not_3_out, in_2[2]);
  not not_4 (not_4_out, in_2[3]);
  not not_5 (not_5_out, in_2[0]);
  not not_6 (not_6_out, in_2[1]);
  not not_7 (not_7_out, in_1[2]);
  not not_8 (not_8_out, in_1[1]);
  not not_9 (not_9_out, in_1[0]);
  and addu (addu_out, in_1[1], not_9_out, in_2[5], not_1_out, not_7_out, not_4_out, not_3_out, not_6_out, in_2[0]);
  and subu (subu_out, in_1[1], not_9_out, in_2[5], not_1_out, not_7_out, not_4_out, not_3_out, in_2[1], in_2[0]);
  and lw_sw (lw_sw_out, not_8_out, not_7_out, not_9_out);
  and beq (beq_out, not_8_out, not_7_out, in_1[0]);
  and ori (ori_out, in_1[1], not_7_out, in_1[0]);
  and Lui_sll (Lui_sll_out, in_1[2], not_8_out, not_9_out);
  // AND_Gate j has open pins: in0=not_8_out, in1=not_7_out, in2=not_9_out, out=open
  buf or_1 (out_3[2], Lui_sll_out);  // OR_Gate
  or or_2 (out_3[1], addu_out, subu_out, lw_sw_out, beq_out);
  or or_3 (out_3[0], beq_out, ori_out, subu_out);

  // Notes on the sheet:
  //   ALUctr2
  //   ALUctr1
  //   ALUctr0
endmodule

module \Lui扩展板  (
  input  [15:0] in_1,
  output [31:0] out_2
);


  assign out_2 = {in_1, {16{1'b0}}};
endmodule

module \ori扩展板  (
  input  [15:0] in_1,
  output [31:0] out_2
);

  assign out_2 = {{16{1'b0}}, in_1};  // Bit_Extender bit_extender_1
endmodule

module extender (
  input  [1:0] in_1,
  input  [15:0] in_2,
  input  [31:0] in_3,
  output [31:0] out_4
);

  wire [31:0] bit_extender_1_out;

  assign bit_extender_1_out = {{16{1'b0}}, in_2};  // Bit_Extender bit_extender_1
  Multiplexer #(.select(2), .width(32)) multiplexer_1 (
    .in0(in_3), .in1(bit_extender_1_out), .in2({in_2, {16{1'b0}}}), .out(out_4), .sel(in_1));  // open: in3, en
endmodule

module \移位器  (
  input  [31:0] in_1,
  input  [4:0] in_2,
  output [31:0] out_3
);

  wire undriven;
  wire [31:0] demultiplexer_1_out0, demultiplexer_1_out1, demultiplexer_2_out0, demultiplexer_2_out1,
       demultiplexer_3_out0, demultiplexer_3_out1, demultiplexer_4_out0, demultiplexer_4_out1,
       demultiplexer_5_out0, demultiplexer_5_out1, or_1_out, or_2_out, or_3_out, or_4_out;

  Demultiplexer #(.width(32)) demultiplexer_1 (
    .out0(demultiplexer_1_out0), .out1(demultiplexer_1_out1), .in(in_1), .sel(in_2[0]), .en(undriven));
  Demultiplexer #(.width(32)) demultiplexer_2 (
    .out0(demultiplexer_2_out0), .out1(demultiplexer_2_out1), .in(or_1_out), .sel(in_2[1]));  // open: en
  assign or_1_out = {demultiplexer_1_out1[30:0], 1'b0} | demultiplexer_1_out0;  // OR_Gate or_1, 32 bits wide
  assign or_2_out = {demultiplexer_2_out1[29:0], 2'b00} | demultiplexer_2_out0;  // OR_Gate or_2, 32 bits wide
  Demultiplexer #(.width(32)) demultiplexer_3 (
    .out0(demultiplexer_3_out0), .out1(demultiplexer_3_out1), .in(or_2_out), .sel(in_2[2]));  // open: en
  assign or_3_out = {demultiplexer_3_out1[27:0], 4'b0000} | demultiplexer_3_out0;  // OR_Gate or_3, 32 bits wide
  Demultiplexer #(.width(32)) demultiplexer_4 (
    .out0(demultiplexer_4_out0), .out1(demultiplexer_4_out1), .in(or_3_out), .sel(in_2[3]));  // open: en
  assign or_4_out = {demultiplexer_4_out1[23:0], {8{1'b0}}} | demultiplexer_4_out0;  // OR_Gate or_4, 32 bits wide
  Demultiplexer #(.width(32)) demultiplexer_5 (
    .out0(demultiplexer_5_out0), .out1(demultiplexer_5_out1), .in(or_4_out), .sel(in_2[4]));  // open: en
  assign out_3 = {demultiplexer_5_out1[15:0], {16{1'b0}}} | demultiplexer_5_out0;  // OR_Gate or_5, 32 bits wide
endmodule

module \sll扩展板  (
  input  [31:0] in_1,
  input  [4:0] in_2,
  output [31:0] out_3
);

  \移位器  \u_移位器_1  (.in_1(in_1), .in_2(in_2), .out_3(out_3));
endmodule

module special (
  input  [5:0] in_1,
  output out_2,
  output out_3
);

  wire and_1_out, and_2_out, not_1_out, not_2_out, not_3_out, not_4_out, not_5_out, not_6_out;

  not not_1 (not_1_out, in_1[5]);
  not not_2 (not_2_out, in_1[3]);
  not not_3 (not_3_out, in_1[4]);
  not not_4 (not_4_out, in_1[1]);
  not not_5 (not_5_out, in_1[2]);
  not not_6 (not_6_out, in_1[0]);
  and specila (out_2, not_1_out, not_3_out, not_2_out, not_5_out, not_4_out, not_6_out);
  and and_1 (and_1_out, in_1[5], not_3_out, not_2_out, not_5_out, not_4_out, in_1[0]);
  and and_2 (and_2_out, in_1[5], not_3_out, not_2_out, not_5_out, in_1[1], in_1[0]);
  or or_1 (out_3, and_1_out, and_2_out);
endmodule
