// Logisim project CPUimp2.01_jal.circ as structural Verilog: 16 circuits, main circuit grf
module grf (
  input  [4:0] in_1,
  input  in_2,
  input  in_3,
  input  [4:0] in_4,
  input  [4:0] in_5,
  input  [31:0] in_6,
  input  in_7,
  output [31:0] out_8,
  output [31:0] out_9
);

  wire [31:0] R0, R1, R2, R3, R4, R5, R6, R7, R8, R9, R10, R11, R12, R13, R14, R15, R16, R17, R18, R19, R20,
       R21, R22, R23, R24, R25, R26, R27, R28, R29, R30, R31, W0, W1, W2, W3, W4, W5, W6, W7, W8, W9, W10,
       W11, W12, W13, W14, W15, W16, W17, W18, W19, W20, W21, W22, W23, W24, W25, W26, W27, W28, W29, W30,
       W31;

  Register #(.width(32)) register_1 (.D(W0), .en(in_3), .Q(R0), .clk(in_2), .clr(in_7));
  Register #(.width(32)) register_2 (.D(W4), .en(in_3), .Q(R4), .clk(in_2), .clr(in_7));
  Register #(.width(32)) register_3 (.D(W8), .en(in_3), .Q(R8), .clk(in_2), .clr(in_7));
  Register #(.width(32)) register_4 (.D(W12), .en(in_3), .Q(R12), .clk(in_2), .clr(in_7));
  Register #(.width(32)) register_5 (.D(W16), .en(in_3), .Q(R16), .clk(in_2), .clr(in_7));
  Register #(.width(32)) register_6 (.D(W20), .en(in_3), .Q(R20), .clk(in_2), .clr(in_7));
  Register #(.width(32)) register_7 (.D(W24), .en(in_3), .Q(R24), .clk(in_2), .clr(in_7));
  Register #(.width(32)) register_8 (.D(W28), .en(in_3), .Q(R28), .clk(in_2), .clr(in_7));
  Register #(.width(32)) register_9 (.D(W1), .en(in_3), .Q(R1), .clk(in_2), .clr(in_7));
  Register #(.width(32)) register_10 (.D(W5), .en(in_3), .Q(R5), .clk(in_2), .clr(in_7));
  Register #(.width(32)) register_11 (.D(W9), .en(in_3), .Q(R9), .clk(in_2), .clr(in_7));
  Register #(.width(32)) register_12 (.D(W13), .en(in_3), .Q(R13), .clk(in_2), .clr(in_7));
  Register #(.width(32)) register_13 (.D(W17), .en(in_3), .Q(R17), .clk(in_2), .clr(in_7));
  Register #(.width(32)) register_14 (.D(W21), .en(in_3), .Q(R21), .clk(in_2), .clr(in_7));
  Register #(.width(32)) register_15 (.D(W25), .en(in_3), .Q(R25), .clk(in_2), .clr(in_7));
  Register #(.width(32)) register_16 (.D(W29), .en(in_3), .Q(R29), .clk(in_2), .clr(in_7));
  Register #(.width(32)) register_17 (.D(W2), .en(in_3), .Q(R2), .clk(in_2), .clr(in_7));
  Register #(.width(32)) register_18 (.D(W6), .en(in_3), .Q(R6), .clk(in_2), .clr(in_7));
  Register #(.width(32)) register_19 (.D(W10), .en(in_3), .Q(R10), .clk(in_2), .clr(in_7));
  Register #(.width(32)) register_20 (.D(W14), .en(in_3), .Q(R14), .clk(in_2), .clr(in_7));
  Register #(.width(32)) register_21 (.D(W18), .en(in_3), .Q(R18), .clk(in_2), .clr(in_7));
  Register #(.width(32)) register_22 (.D(W22), .en(in_3), .Q(R22), .clk(in_2), .clr(in_7));
  Register #(.width(32)) register_23 (.D(W26), .en(in_3), .Q(R26), .clk(in_2), .clr(in_7));
  Register #(.width(32)) register_24 (.D(W30), .en(in_3), .Q(R30), .clk(in_2), .clr(in_7));
  Register #(.width(32)) register_25 (.D(W3), .en(in_3), .Q(R3), .clk(in_2), .clr(in_7));
  Register #(.width(32)) register_26 (.D(W7), .en(in_3), .Q(R7), .clk(in_2), .clr(in_7));
  Register #(.width(32)) register_27 (.D(W11), .en(in_3), .Q(R11), .clk(in_2), .clr(in_7));
  Register #(.width(32)) register_28 (.D(W15), .en(in_3), .Q(R15), .clk(in_2), .clr(in_7));
  Register #(.width(32)) register_29 (.D(W19), .en(in_3), .Q(R19), .clk(in_2), .clr(in_7));
  Register #(.width(32)) register_30 (.D(W23), .en(in_3), .Q(R23), .clk(in_2), .clr(in_7));
  Register #(.width(32)) register_31 (.D(W27), .en(in_3), .Q(R27), .clk(in_2), .clr(in_7));
  Register #(.width(32)) register_32 (.D(W31), .en(in_3), .Q(R31), .clk(in_2), .clr(in_7));
  Multiplexer #(.select(5), .width(32)) multiplexer_1 (
    .in0({32{1'b0}}), .in1(R1), .in2(R2), .in3(R3), .in4(R4), .in5(R5), .in6(R6), .in7(R7), .in8(R8),
    .in9(R9), .in10(R10), .in11(R11), .in12(R12), .in13(R13), .in14(R14), .in15(R15), .in16(R16), .in17(R17),
    .in18(R18), .in19(R19), .in20(R20), .in21(R21), .in22(R22), .in23(R23), .in24(R24), .in25(R25),
    .in26(R26), .in27(R27), .in28(R28), .in29(R29), .in30(R30), .in31(R31), .out(out_9), .sel(in_4));  // open: en
  Multiplexer #(.select(5), .width(32)) multiplexer_2 (
    .in0({32{1'b0}}), .in1(R1), .in2(R2), .in3(R3), .in4(R4), .in5(R5), .in6(R6), .in7(R7), .in8(R8),
    .in9(R9), .in10(R10), .in11(R11), .in12(R12), .in13(R13), .in14(R14), .in15(R15), .in16(R16), .in17(R17),
    .in18(R18), .in19(R19), .in20(R20), .in21(R21), .in22(R22), .in23(R23), .in24(R24), .in25(R25),
    .in26(R26), .in27(R27), .in28(R28), .in29(R29), .in30(R30), .in31(R31), .out(out_8), .sel(in_1));  // open: en
  Demultiplexer #(.select(5), .width(32), .tristate("true")) demultiplexer_1 (
    .out0(W0), .out1(W1), .out2(W2), .out3(W3), .out4(W4), .out5(W5), .out6(W6), .out7(W7), .out8(W8),
    .out9(W9), .out10(W10), .out11(W11), .out12(W12), .out13(W13), .out14(W14), .out15(W15), .out16(W16),
    .out17(W17), .out18(W18), .out19(W19), .out20(W20), .out21(W21), .out22(W22), .out23(W23), .out24(W24),
    .out25(W25), .out26(W26), .out27(W27), .out28(W28), .out29(W29), .out30(W30), .out31(W31), .in(in_6),
    .sel(in_5));  // open: en

  // Other names for the same wires on the sheet: A1[4:0] = in_1; A2[4:0] = in_4; A3[4:0] = in_5; clk = in_2;
  //   en = in_3; reset = in_7; WD[31:0] = in_6
endmodule

module main (
  input  in_1,
  output [31:0] out_2,
  output out_3,
  output [4:0] out_4,
  output [31:0] out_5,
  output out_6,
  output [4:0] out_7,
  output [31:0] out_8
);

  wire ALUSrc, ALUzero, branch, clock_1_out, clock_2_out, clock_3_out, jal, jr, jump, MemtoReg, RegDst;
  wire [1:0] alu_1_out_5, EXT;
  wire [2:0] ALUctrl;
  wire [4:0] multiplexer_1_out, \分线器_1_out_3 , \分线器_1_out_4 , \分线器_1_out_5 ;
  wire [5:0] func, OP;
  wire [15:0] imme;
  wire [24:0] alu_1_out_5_2;
  wire [25:0] INDEX;
  wire [31:0] adder_1_out, bit_extender_1_out, dm_1_out_6, extender_1_out_4, multiplexer_3_out,
       multiplexer_5_out, npc_1_out_9, RD1, register_1_q;

  Clock clock_1 (.out(clock_1_out));
  NPC npc_1 (
    .in_1(branch), .in_3(ALUzero), .in_4(jump), .in_7(register_1_q), .in_5(INDEX), .in_2(imme), .in_6(jr),
    .in_8(RD1), .out_9(npc_1_out_9));
  Register #(.width(32)) register_1 (.D(npc_1_out_9), .Q(register_1_q), .clk(clock_1_out), .clr(in_1));  // open: en
  \主译码器  \u_主译码器_1  (
    .in_1(OP), .in_2(func), .MemtoReg(MemtoReg), .Memwrite(out_6), .branch(branch), .out_6(ALUctrl),
    .ALUSrc(ALUSrc), .RegDst(RegDst), .RegWrite(out_3), .JUMP(jump), .out_11(EXT), .jal(jal), .jr(jr));
  IM im_1 (.in_1(register_1_q), .out_2(out_2));
  \分线器  \u_分线器_1  (
    .in_1(out_2), .out_2(OP), .out_3(\分线器_1_out_3 ), .out_4(\分线器_1_out_4 ), .out_5(\分线器_1_out_5 ),
    .out_6(func), .out_7(imme), .out_8(INDEX));  // open: out_9
  Adder #(.width(32)) adder_1 (.a(register_1_q), .b(32'h4), .out(adder_1_out));  // open: cin, cout
  Multiplexer #(.width(5)) multiplexer_1 (
    .in0(\分线器_1_out_4 ), .in1(\分线器_1_out_5 ), .out(multiplexer_1_out), .sel(RegDst));  // open: en
  Multiplexer #(.width(5)) multiplexer_2 (
    .in0(multiplexer_1_out), .in1({5{1'b1}}), .out(out_4), .sel(jal));  // open: en
  Clock clock_2 (.out(clock_2_out));
  grf grf_1 (
    .in_1(\分线器_1_out_3 ), .in_4(\分线器_1_out_4 ), .in_5(out_4), .in_6(out_5), .out_8(RD1), .out_9(out_8),
    .in_2(clock_2_out), .in_3(out_3), .in_7(in_1));
  assign bit_extender_1_out = {{16{imme[15]}}, imme};  // Bit_Extender bit_extender_1
  Multiplexer #(.width(32)) multiplexer_3 (
    .in0(out_8), .in1(bit_extender_1_out), .out(multiplexer_3_out), .sel(ALUSrc));  // open: en
  Multiplexer #(.width(32)) multiplexer_4 (
    .in0(multiplexer_5_out), .in1(adder_1_out), .out(out_5), .sel(jal));  // open: en
  extender extender_1 (.in_3(multiplexer_3_out), .in_2(imme), .in_1(EXT), .out_4(extender_1_out_4));
  ALU alu_1 (
    .in_2(RD1), .in_3(extender_1_out_4), .out_4(ALUzero), .out_5({alu_1_out_5_2, out_7, alu_1_out_5}),
    .in_1(ALUctrl));
  Clock clock_3 (.out(clock_3_out));
  DM dm_1 (
    .in_3({alu_1_out_5_2, out_7, alu_1_out_5}), .in_4(out_8), .out_6(dm_1_out_6), .in_1(clock_3_out),
    .in_5(in_1), .in_2(out_6));
  Multiplexer #(.width(32)) multiplexer_5 (
    .in0({alu_1_out_5_2, out_7, alu_1_out_5}), .in1(dm_1_out_6), .out(multiplexer_5_out), .sel(MemtoReg));  // open: en

  // Other names for the same wires on the sheet: MemAddr[4:0] = out_7; instr[31:0] = out_2; MemData[31:0] = out_8;
  //   MemWrite = out_6; RegAddr[4:0] = out_4; RegData[31:0] = out_5; RegWrite = out_3; reset = in_1

  // Notes on the sheet:
  //   pc
  //   IM
  //   RD
endmodule

module IM (
  input  [31:0] in_1,
  output [31:0] out_2
);

  ROM #(.addrWidth(5), .dataWidth(32)) rom_1 (.addr(in_1[6:2]), .data(out_2));  // open: sel

  // Notes on the sheet:
  //   contents of rom_1 (hex, n*v repeats v):
  //   35290001 354a0002 c000c09 35ad0005 35ce0006 c000c0c 0 0 8000c0f 358c0004 356b0003 3e00008 36310001
  //   36520002 3e00008
endmodule

module \分线器  (
  input  [31:0] in_1,
  output [5:0] out_2,
  output [4:0] out_3,
  output [4:0] out_4,
  output [4:0] out_5,
  output [5:0] out_6,
  output [15:0] out_7,
  output [25:0] out_8,
  output [4:0] out_9
);


  assign out_2 = in_1[31:26];
  assign out_3 = in_1[25:21];
  assign out_4 = in_1[20:16];
  assign out_5 = in_1[15:11];
  assign out_6 = in_1[5:0];
  assign out_7 = in_1[15:0];
  assign out_8 = in_1[25:0];
  assign out_9 = in_1[10:6];
endmodule

module ALU (
  input  [2:0] in_1,
  input  [31:0] in_2,
  input  [31:0] in_3,
  output out_4,
  output [31:0] out_5
);

  wire comparator_1_eq;
  wire [31:0] adder_1_out, and_1_out, bit_extender_1_out, or_1_out, subtractor_1_out, xor_1_out;

  assign and_1_out = in_2 & in_3;  // AND_Gate and_1, 32 bits wide
  assign or_1_out = in_2 | in_3;  // OR_Gate or_1, 32 bits wide
  Adder #(.width(32)) adder_1 (.a(in_2), .b(in_3), .out(adder_1_out));  // open: cin, cout
  Subtractor #(.width(32)) subtractor_1 (.a(in_2), .b(in_3), .out(subtractor_1_out));  // open: bin, bout
  assign xor_1_out = in_2 ^ in_3;  // XOR_Gate xor_1, 32 bits wide
  Comparator #(.width(32), .mode("unsigned")) comparator_1 (.a(in_2), .b(in_3), .eq(comparator_1_eq));  // open: gt, lt
  assign bit_extender_1_out = {{31{1'b0}}, comparator_1_eq};  // Bit_Extender bit_extender_1
  Multiplexer #(.select(3), .width(32)) multiplexer_1 (
    .in0(and_1_out), .in1(or_1_out), .in2(adder_1_out), .in3(subtractor_1_out), .in4(xor_1_out),
    .in5(bit_extender_1_out), .out(out_5), .sel(in_1));  // open: in6, in7, en
  Comparator #(.width(32), .mode("unsigned")) comparator_2 (.a(out_5), .b({32{1'b0}}), .eq(out_4));  // open: gt, lt

  // Other names for the same wires on the sheet: dataA[31:0] = in_2; dataB[31:0] = in_3; select[2:0] = in_1
endmodule

module DM (
  input  in_1,
  input  in_2,
  input  [31:0] in_3,
  input  [31:0] in_4,
  input  in_5,
  output [31:0] out_6
);

  RAM #(.addrWidth(5), .dataWidth(32), .bus("separate")) ram_1 (
    .addr(in_3[6:2]), .din(in_4), .data(out_6), .str(in_2), .clk(in_1), .clr(in_5));  // open: sel, ld

  // Other names for the same wires on the sheet: clk = in_1; write = in_2
endmodule

module JPC (
  input  [31:0] in_1,
  input  [25:0] in_2,
  output [31:0] out_3
);


  assign out_3 = {in_1[31:28], in_2, 2'b00};
endmodule

module \主译码器  (
  input  [5:0] in_1,
  input  [5:0] in_2,
  output MemtoReg,
  output Memwrite,
  output branch,
  output [2:0] out_6,
  output ALUSrc,
  output RegDst,
  output RegWrite,
  output JUMP,
  output [1:0] out_11,
  output jal,
  output jr
);

  wire J_out, liu_out, not_1_out, not_2_out, not_3_out, not_4_out, not_5_out, not_6_out, ori_out,
       special_1_out_2, special_1_out_3;
  wire [2:0] ALUop0_out;

  not not_1 (not_1_out, in_1[5]);
  not not_2 (not_2_out, in_1[3]);
  not not_3 (not_3_out, in_1[4]);
  not not_4 (not_4_out, in_1[1]);
  not not_5 (not_5_out, in_1[2]);
  special special_1 (.in_1(in_2), .out_2(special_1_out_2), .out_3(special_1_out_3));
  not not_6 (not_6_out, in_1[0]);
  and addu_subu (RegDst, not_1_out, not_3_out, not_2_out, special_1_out_3, not_5_out, not_4_out, not_6_out);
  and LW (MemtoReg, in_1[5], not_3_out, not_2_out, not_5_out, in_1[1], in_1[0]);
  and SW (Memwrite, in_1[5], not_3_out, in_1[3], not_5_out, in_1[1], in_1[0]);
  and beq (branch, not_1_out, not_3_out, not_2_out, in_1[2], not_4_out, not_6_out);
  and J (J_out, not_1_out, not_3_out, not_2_out, not_5_out, in_1[1], not_6_out);
  and ori (ori_out, not_1_out, not_3_out, in_1[3], in_1[2], not_4_out, in_1[0]);
  and liu (liu_out, not_1_out, not_3_out, in_1[3], in_1[2], in_1[1], in_1[0]);
  and u_jal (jal, not_1_out, not_3_out, not_2_out, not_5_out, in_1[1], in_1[0]);
  and u_jr (jr, not_1_out, not_3_out, not_2_out, not_5_out, not_4_out, not_6_out, special_1_out_2);
  or or_1 (ALUSrc, Memwrite, MemtoReg);
  or or_2 (RegWrite, RegDst, ori_out, jal, liu_out, MemtoReg);
  or or_3 (JUMP, jal, J_out);
  buf ALUop2 (ALUop0_out[2], liu_out);  // OR_Gate
  or ALUop1 (ALUop0_out[1], RegDst, ori_out);
  or ALUop0 (ALUop0_out[0], branch, ori_out);
  buf ext1 (out_11[1], liu_out);  // OR_Gate
  buf ext0 (out_11[0], ori_out);  // OR_Gate
  \ALU译码器  \alu译码器_1  (.in_1(ALUop0_out), .in_2(in_2), .out_3(out_6));

  // Other names for the same wires on the sheet: ALUctr[2:0] = out_6; func[5:0] = in_2
endmodule

module \ALU译码器  (
  input  [2:0] in_1,
  input  [5:0] in_2,
  output [2:0] out_3
);

  wire addu_out, beq_out, Lui_out, lw_sw_out, not_1_out, not_2_out, not_3_out, not_4_out, not_5_out,
       not_6_out, not_7_out, not_8_out, not_9_out, ori_out, subu_out;

  not not_1 (not_1_out, in_2[4]);
  not not_2 (not_2_out, in_2[5]);
  not not_3 (not_3_out, in_2[2]);
  not not_4 (not_4_out, in_2[3]);
  not not_5 (not_5_out, in_2[0]);
  not not_6 (not_6_out, in_2[1]);
  not not_7 (not_7_out, in_1[2]);
  not not_8 (not_8_out, in_1[1]);
  not not_9 (not_9_out, in_1[0]);
  and addu (addu_out, in_1[1], not_9_out, in_2[5], not_1_out, not_7_out, not_4_out, not_3_out, not_6_out, in_2[0]);
  and subu (subu_out, in_1[1], not_9_out, in_2[5], not_1_out, not_7_out, not_4_out, not_3_out, in_2[1], in_2[0]);
  and lw_sw (lw_sw_out, not_8_out, not_7_out, not_9_out);
  and beq (beq_out, not_8_out, not_7_out, in_1[0]);
  and ori (ori_out, in_1[1], not_7_out, in_1[0]);
  and Lui (Lui_out, in_1[2], not_8_out, not_9_out);
  // AND_Gate j has open pins: in0=not_8_out, in1=not_7_out, in2=not_9_out, out=open
  buf or_1 (out_3[2], Lui_out);  // OR_Gate
  or or_2 (out_3[1], addu_out, subu_out, lw_sw_out, beq_out);
  or or_3 (out_3[0], beq_out, ori_out, subu_out);

  // Notes on the sheet:
  //   ALUctr2
  //   ALUctr1
  //   ALUctr0
endmodule

module \Lui扩展板  (
  input  [15:0] in_1,
  output [31:0] out_2
);


  assign out_2 = {in_1, {16{1'b0}}};
endmodule

module \ori扩展板  (
  input  [15:0] in_1,
  output [31:0] out_2
);

  assign out_2 = {{16{1'b0}}, in_1};  // Bit_Extender bit_extender_1
endmodule

module extender (
  input  [1:0] in_1,
  input  [15:0] in_2,
  input  [31:0] in_3,
  output [31:0] out_4
);

  wire [31:0] bit_extender_1_out;

  assign bit_extender_1_out = {{16{1'b0}}, in_2};  // Bit_Extender bit_extender_1
  Multiplexer #(.select(2), .width(32)) multiplexer_1 (
    .in0(in_3), .in1(bit_extender_1_out), .in2({in_2, {16{1'b0}}}), .out(out_4), .sel(in_1));  // open: in3, en
endmodule

module special (
  input  [5:0] in_1,
  output out_2,
  output out_3
);

  wire and_2_out, and_3_out, not_1_out, not_2_out, not_3_out, not_4_out, not_5_out, not_6_out;

  not not_1 (not_1_out, in_1[5]);
  not not_2 (not_2_out, in_1[3]);
  not not_3 (not_3_out, in_1[4]);
  not not_4 (not_4_out, in_1[1]);
  not not_5 (not_5_out, in_1[2]);
  not not_6 (not_6_out, in_1[0]);
  and and_1 (out_2, not_1_out, not_3_out, in_1[3], not_5_out, not_4_out, not_6_out);
  and and_2 (and_2_out, in_1[5], not_3_out, not_2_out, not_5_out, not_4_out, in_1[0]);
  and and_3 (and_3_out, in_1[5], not_3_out, not_2_out, not_5_out, in_1[1], in_1[0]);
  or or_1 (out_3, and_2_out, and_3_out);
endmodule

module \sb扩展  (
  input  [31:0] in_1,
  input  [31:0] in_2,
  input  [31:0] in_3,
  output [31:0] out_4
);

  Multiplexer #(.select(2), .width(32)) multiplexer_1 (
    .in0({in_3[31:8], in_2[7:0]}), .in1({in_3[31:16], in_2[7:0], in_3[7:0]}),
    .in2({in_3[31:24], in_2[7:0], in_3[15:0]}), .in3({in_2[7:0], in_3[23:0]}), .out(out_4), .sel(in_1[1:0]));  // open: en

  // Other names for the same wires on the sheet: sb_select[1:0] = in_1[1:0]

  // Notes on the sheet:
  //   RD2
  //   Predata
  //   A
  //   outPUT
endmodule

module \lb扩展  (
  input  [31:0] in_1,
  input  [31:0] in_2,
  output [31:0] out_3
);

  Multiplexer #(.select(2), .width(8)) multiplexer_1 (
    .in0(in_2[7:0]), .in1(in_2[15:8]), .in2(in_2[23:16]), .in3(in_2[31:24]), .out(out_3[7:0]), .sel(in_1[1:0]));  // open: en

  assign out_3[31:8] = {24{1'b0}};

  // Notes on the sheet:
  //   A
  //   Data
endmodule

module NPC (
  input  in_1,
  input  [15:0] in_2,
  input  in_3,
  input  in_4,
  input  [25:0] in_5,
  input  in_6,
  input  [31:0] in_7,
  input  [31:0] in_8,
  output [31:0] out_9
);

  wire PcSrc;
  wire [31:0] adder_1_out, adder_2_out, bit_extender_1_out, jpc_1_out_3, multiplexer_1_out,
       multiplexer_2_out, shifter_1_out;

  Multiplexer #(.width(32)) multiplexer_1 (
    .in0(adder_1_out), .in1(adder_2_out), .out(multiplexer_1_out), .sel(PcSrc));  // open: en
  Multiplexer #(.width(32)) multiplexer_2 (
    .in0(multiplexer_1_out), .in1(jpc_1_out_3), .out(multiplexer_2_out), .sel(in_4));  // open: en
  Multiplexer #(.width(32)) multiplexer_3 (.in0(multiplexer_2_out), .in1(in_8), .out(out_9), .sel(in_6));  // open: en
  JPC jpc_1 (.out_3(jpc_1_out_3), .in_2(in_5), .in_1(in_7));
  Adder #(.width(32)) adder_1 (.a(in_7), .b(32'h4), .out(adder_1_out));  // open: cin, cout
  assign bit_extender_1_out = {{16{in_2[15]}}, in_2};  // Bit_Extender bit_extender_1
  and and_1 (PcSrc, in_1, in_3);
  Shifter #(.width(32)) shifter_1 (.in(bit_extender_1_out), .\dist (5'b00010), .out(shifter_1_out));
  Adder #(.width(32)) adder_2 (.a(shifter_1_out), .b(adder_1_out), .out(adder_2_out));  // open: cin, cout

  // Other names for the same wires on the sheet: imm[15:0] = in_2; index[25:0] = in_5; jr = in_6; jump = in_4
endmodule
