// Logisim project fib challenge.circ as structural Verilog: 8 circuits, main circuit 矩阵乘法
module \矩阵乘法  (
  input  [31:0] in_1,
  input  [31:0] in_2,
  input  [31:0] in_3,
  input  [31:0] in_4,
  input  [31:0] in_5,
  input  [31:0] in_6,
  input  [31:0] in_7,
  input  [31:0] in_8,
  output [31:0] out_9,
  output [31:0] out_10,
  output [31:0] out_11,
  output [31:0] out_12
);

  wire [31:0] multiplier_1_out, multiplier_2_out, multiplier_3_out, multiplier_4_out, multiplier_5_out,
       multiplier_6_out, multiplier_7_out, multiplier_8_out;

  Multiplier #(.width(32)) multiplier_1 (.a(in_1), .b(in_5), .out(multiplier_1_out));  // open: cin, cout
  Multiplier #(.width(32)) multiplier_2 (.a(in_2), .b(in_7), .out(multiplier_2_out));  // open: cin, cout
  Multiplier #(.width(32)) multiplier_3 (.a(in_1), .b(in_6), .out(multiplier_3_out));  // open: cin, cout
  Multiplier #(.width(32)) multiplier_4 (.a(in_2), .b(in_8), .out(multiplier_4_out));  // open: cin, cout
  Multiplier #(.width(32)) multiplier_5 (.a(in_3), .b(in_5), .out(multiplier_5_out));  // open: cin, cout
  Multiplier #(.width(32)) multiplier_6 (.a(in_4), .b(in_7), .out(multiplier_6_out));  // open: cin, cout
  Multiplier #(.width(32)) multiplier_7 (.a(in_3), .b(in_6), .out(multiplier_7_out));  // open: cin, cout
  Multiplier #(.width(32)) multiplier_8 (.a(in_4), .b(in_8), .out(multiplier_8_out));  // open: cin, cout
  Adder #(.width(32)) adder_1 (.a(multiplier_1_out), .b(multiplier_2_out), .out(out_9));  // open: cin, cout
  Adder #(.width(32)) adder_2 (.a(multiplier_3_out), .b(multiplier_4_out), .out(out_10));  // open: cin, cout
  Adder #(.width(32)) adder_3 (.a(multiplier_5_out), .b(multiplier_6_out), .out(out_11));  // open: cin, cout
  Adder #(.width(32)) adder_4 (.a(multiplier_7_out), .b(multiplier_8_out), .out(out_12));  // open: cin, cout

  // Other names for the same wires on the sheet: in_a11[31:0] = in_1; in_a12[31:0] = in_2; in_a21[31:0] = in_3;
  //   in_a22[31:0] = in_4; in_b11[31:0] = in_5; in_b12[31:0] = in_6; in_b21[31:0] = in_7; in_b22[31:0] = in_8

  // Notes on the sheet:
  //   out c11
  //   out c12
  //   out c21
  //   out c22
endmodule

module \矩阵寄存器  (
  input  [31:0] in_1,
  input  [31:0] in_2,
  input  [31:0] in_3,
  input  [31:0] in_4,
  input  in_5,
  input  in_6,
  input  in_7,
  output [31:0] out_8,
  output [31:0] out_9,
  output [31:0] out_10,
  output [31:0] out_11
);

  Register #(.width(32)) register_1 (.D(in_1), .en(in_5), .Q(out_8), .clk(in_6), .clr(in_7));
  Register #(.width(32)) register_2 (.D(in_2), .en(in_5), .Q(out_9), .clk(in_6), .clr(in_7));
  Register #(.width(32)) register_3 (.D(in_3), .en(in_5), .Q(out_10), .clk(in_6), .clr(in_7));
  Register #(.width(32)) register_4 (.D(in_4), .en(in_5), .Q(out_11), .clk(in_6), .clr(in_7));
endmodule

module \矩阵选择  (
  input  [31:0] in_1,
  input  [31:0] in_2,
  input  [31:0] in_3,
  input  [31:0] in_4,
  input  [31:0] in_5,
  input  [31:0] in_6,
  input  [31:0] in_7,
  input  [31:0] in_8,
  input  in_9,
  output [31:0] out_10,
  output [31:0] out_11,
  output [31:0] out_12,
  output [31:0] out_13
);

  Multiplexer #(.width(32)) multiplexer_1 (.in0(in_1), .in1(in_5), .out(out_10), .sel(in_9));  // open: en
  Multiplexer #(.width(32)) multiplexer_2 (.in0(in_2), .in1(in_6), .out(out_11), .sel(in_9));  // open: en
  Multiplexer #(.width(32)) multiplexer_3 (.in0(in_3), .in1(in_7), .out(out_12), .sel(in_9));  // open: en
  Multiplexer #(.width(32)) multiplexer_4 (.in0(in_4), .in1(in_8), .out(out_13), .sel(in_9));  // open: en

  // Other names for the same wires on the sheet: a11[31:0] = in_1; a12[31:0] = in_2; a21[31:0] = in_3;
  //   a22[31:0] = in_4; b11[31:0] = in_5; b12[31:0] = in_6; b21[31:0] = in_7; b22[31:0] = in_8
endmodule

module \初值  (
  output [31:0] out_1,
  output [31:0] out_2,
  output [31:0] out_3,
  output [31:0] out_4
);


  assign out_1 = 32'h1;
  assign out_2 = 32'h1;
  assign out_3 = 32'h1;
  assign out_4 = {32{1'b0}};
endmodule

module \单位矩阵  (
  output [31:0] out_1,
  output [31:0] out_2,
  output [31:0] out_3,
  output [31:0] out_4
);


  assign out_1 = 32'h1;
  assign out_2 = {32{1'b0}};
  assign out_3 = {32{1'b0}};
  assign out_4 = 32'h1;
endmodule

module \计数逻辑  (
  input  [31:0] in_1,
  input  in_2,
  input  in_3,
  output n_low,
  output freeze
);

  wire comparator_1_eq, \initial ;
  wire [31:0] multiplexer_2_out, n, shifter_1_out;

  Counter #(.width(1), .max('h1), .ongoal("stay")) counter_1 (
    .Q(\initial ), .clk(in_2), .clr(in_3));  // open: load, D, count, carry
  Shifter #(.width(32), .shift("lr")) shifter_1 (.in(n), .\dist (5'b00001), .out(shifter_1_out));
  Bit_Extender #(.in_width(32), .out_width(1)) bit_extender_1 (.in(n), .out(n_low));
  Comparator #(.width(32), .mode("unsigned")) comparator_1 (
    .a(n), .b({32{1'b0}}), .eq(comparator_1_eq));  // open: gt, lt
  Multiplexer multiplexer_1 (.in0(1'b0), .in1(comparator_1_eq), .out(freeze), .sel(\initial ));  // open: en
  Multiplexer #(.width(32)) multiplexer_2 (
    .in0(in_1), .in1(shifter_1_out), .out(multiplexer_2_out), .sel(\initial ));  // open: en
  Register #(.width(32)) register_1 (.D(multiplexer_2_out), .Q(n), .clk(in_2), .clr(in_3));  // open: en
endmodule

module \计算单元  (
  input  in_1,
  input  in_2,
  input  in_3,
  input  in_4,
  output [31:0] out_5
);

  wire enable, \initial ;
  wire [31:0] a11, a12, a21, a22, s11, s12, s21, s22, \初值_1_out_1 , \初值_1_out_2 , \初值_1_out_3 , \初值_1_out_4 ,
       \单位矩阵_1_out_1 , \单位矩阵_1_out_2 , \单位矩阵_1_out_3 , \单位矩阵_1_out_4 , \单位矩阵_2_out_1 , \单位矩阵_2_out_2 ,
       \单位矩阵_2_out_3 , \单位矩阵_2_out_4 , \矩阵乘法_1_out_9 , \矩阵乘法_1_out_10 , \矩阵乘法_1_out_11 , \矩阵乘法_1_out_12 ,
       \矩阵乘法_2_out_9 , \矩阵乘法_2_out_10 , \矩阵乘法_2_out_11 , \矩阵乘法_2_out_12 , \矩阵选择_1_out_10 , \矩阵选择_1_out_11 ,
       \矩阵选择_1_out_12 , \矩阵选择_1_out_13 , \矩阵选择_2_out_10 , \矩阵选择_2_out_11 , \矩阵选择_2_out_12 , \矩阵选择_2_out_13 ,
       \矩阵选择_3_out_10 , \矩阵选择_3_out_11 , \矩阵选择_3_out_12 , \矩阵选择_3_out_13 ;

  not not_1 (enable, in_3);
  Counter #(.width(1), .max('h1), .ongoal("stay")) counter_1 (
    .Q(\initial ), .clk(in_1), .clr(in_4));  // open: load, D, count, carry
  \单位矩阵  \u_单位矩阵_1  (.out_1(\单位矩阵_1_out_1 ), .out_2(\单位矩阵_1_out_2 ), .out_3(\单位矩阵_1_out_3 ), .out_4(\单位矩阵_1_out_4 ));
  \矩阵乘法  \u_矩阵乘法_1  (
    .in_1(a11), .in_2(a12), .in_3(a21), .in_4(a22), .in_5(a11), .in_6(a12), .in_7(a21), .in_8(a22),
    .out_9(\矩阵乘法_1_out_9 ), .out_10(\矩阵乘法_1_out_10 ), .out_11(\矩阵乘法_1_out_11 ), .out_12(\矩阵乘法_1_out_12 ));
  \单位矩阵  \u_单位矩阵_2  (.out_1(\单位矩阵_2_out_1 ), .out_2(\单位矩阵_2_out_2 ), .out_3(\单位矩阵_2_out_3 ), .out_4(\单位矩阵_2_out_4 ));
  \矩阵选择  \u_矩阵选择_1  (
    .in_1(\单位矩阵_1_out_1 ), .in_2(\单位矩阵_1_out_2 ), .in_3(\单位矩阵_1_out_3 ), .in_4(\单位矩阵_1_out_4 ), .in_5(a11),
    .in_6(a12), .in_7(a21), .in_8(a22), .in_9(in_2), .out_10(\矩阵选择_1_out_10 ), .out_11(\矩阵选择_1_out_11 ),
    .out_12(\矩阵选择_1_out_12 ), .out_13(\矩阵选择_1_out_13 ));
  \初值  \u_初值_1  (.out_1(\初值_1_out_1 ), .out_2(\初值_1_out_2 ), .out_3(\初值_1_out_3 ), .out_4(\初值_1_out_4 ));
  \矩阵选择  \u_矩阵选择_2  (
    .in_1(\初值_1_out_1 ), .in_2(\初值_1_out_2 ), .in_3(\初值_1_out_3 ), .in_4(\初值_1_out_4 ),
    .in_5(\矩阵乘法_1_out_9 ), .in_6(\矩阵乘法_1_out_10 ), .in_7(\矩阵乘法_1_out_11 ), .in_8(\矩阵乘法_1_out_12 ),
    .in_9(\initial ), .out_10(\矩阵选择_2_out_10 ), .out_11(\矩阵选择_2_out_11 ), .out_12(\矩阵选择_2_out_12 ),
    .out_13(\矩阵选择_2_out_13 ));
  \矩阵选择  \u_矩阵选择_3  (
    .in_1(\单位矩阵_2_out_1 ), .in_2(\单位矩阵_2_out_2 ), .in_3(\单位矩阵_2_out_3 ), .in_4(\单位矩阵_2_out_4 ), .in_5(s11),
    .in_6(s12), .in_7(s21), .in_8(s22), .in_9(\initial ), .out_10(\矩阵选择_3_out_10 ), .out_11(\矩阵选择_3_out_11 ),
    .out_12(\矩阵选择_3_out_12 ), .out_13(\矩阵选择_3_out_13 ));
  \矩阵乘法  \u_矩阵乘法_2  (
    .in_1(\矩阵选择_3_out_10 ), .in_2(\矩阵选择_3_out_11 ), .in_3(\矩阵选择_3_out_12 ), .in_4(\矩阵选择_3_out_13 ),
    .in_5(\矩阵选择_1_out_10 ), .in_6(\矩阵选择_1_out_11 ), .in_7(\矩阵选择_1_out_12 ), .in_8(\矩阵选择_1_out_13 ),
    .out_9(\矩阵乘法_2_out_9 ), .out_10(\矩阵乘法_2_out_10 ), .out_11(\矩阵乘法_2_out_11 ), .out_12(\矩阵乘法_2_out_12 ));
  \矩阵寄存器  \u_矩阵寄存器_1  (
    .in_1(\矩阵选择_2_out_10 ), .in_2(\矩阵选择_2_out_11 ), .in_3(\矩阵选择_2_out_12 ), .in_4(\矩阵选择_2_out_13 ),
    .in_5(enable), .in_6(in_1), .in_7(in_4), .out_8(a11), .out_9(a12), .out_10(a21), .out_11(a22));
  \矩阵寄存器  \u_矩阵寄存器_2  (
    .in_1(\矩阵乘法_2_out_9 ), .in_2(\矩阵乘法_2_out_10 ), .in_3(\矩阵乘法_2_out_11 ), .in_4(\矩阵乘法_2_out_12 ),
    .in_5(enable), .in_6(in_1), .in_7(in_4), .out_8(s11), .out_9(s12), .out_10(s21), .out_11(s22));
  Multiplexer #(.width(32)) multiplexer_1 (.in0({32{1'b0}}), .in1(s12), .out(out_5), .sel(in_3));  // open: en

  // Other names for the same wires on the sheet: clk = in_1; clr = in_4; freeze = in_3; n_low = in_2
endmodule

module main (
  input  [31:0] in_1,
  output [31:0] out_2
);

  wire clock_1_out, \计数逻辑_1_freeze , \计数逻辑_1_n_low ;

  Clock clock_1 (.out(clock_1_out));
  // Probe on \计数逻辑_1_n_low 
  \计数逻辑  \u_计数逻辑_1  (.in_1(in_1), .in_2(clock_1_out), .in_3(1'b0), .n_low(\计数逻辑_1_n_low ), .freeze(\计数逻辑_1_freeze ));
  // Probe on \计数逻辑_1_freeze 
  \计算单元  \u_计算单元_1  (.in_1(clock_1_out), .in_2(\计数逻辑_1_n_low ), .in_3(\计数逻辑_1_freeze ), .in_4(1'b0), .out_5(out_2));
endmodule
