// Logisim project mod.circ as structural Verilog: 1 circuit, main circuit mod5
module mod5 (
  input  in_1,
  output out_2,
  output out_3,
  output out_4,
  output out_5,
  output out_6
);

  wire and_1_out, and_2_out, and_3_out, and_4_out, and_5_out, and_6_out, and_7_out, and_8_out, and_9_out,
       and_10_out, and_11_out, and_12_out, clock_1_out, not_1_out, not_2_out, not_3_out, not_4_out,
       not_5_out, not_6_out, register_1_q, register_2_q, S0_prime_out, S1_prime_out;
  wire [1:0] cin0_out;

  not not_1 (not_1_out, in_1);
  not not_2 (not_2_out, register_1_q);
  not not_3 (not_3_out, register_2_q);
  and and_1 (and_1_out, not_2_out, register_2_q);
  and and_2 (and_2_out, register_1_q, not_3_out);
  and and_3 (and_3_out, not_2_out, not_3_out, in_1);
  and and_4 (and_4_out, not_2_out, register_2_q, not_1_out);
  and and_5 (and_5_out, register_1_q, not_3_out, not_1_out);
  and and_6 (and_6_out, register_1_q, register_2_q, in_1);
  or S1_prime (S1_prime_out, and_1_out, and_2_out);
  or S0_prime (S0_prime_out, and_3_out, and_4_out, and_5_out, and_6_out);
  Clock clock_1 (.out(clock_1_out));
  Register #(.width(1)) register_1 (.D(S1_prime_out), .Q(register_1_q), .clk(clock_1_out));  // open: en, clr
  Register #(.width(1)) register_2 (.D(S0_prime_out), .Q(register_2_q), .clk(clock_1_out));  // open: en, clr
  not not_4 (not_4_out, in_1);
  not not_5 (not_5_out, register_1_q);
  not not_6 (not_6_out, register_2_q);
  and and_7 (and_7_out, not_5_out, register_2_q);
  and and_8 (and_8_out, register_1_q, not_6_out);
  and and_9 (and_9_out, not_5_out, not_6_out, in_1);
  and and_10 (and_10_out, not_5_out, register_2_q, not_4_out);
  and and_11 (and_11_out, register_1_q, not_6_out, not_4_out);
  and and_12 (and_12_out, register_1_q, register_2_q, in_1);
  or or_1 (cin0_out[1], and_7_out, and_8_out);
  or cin0 (cin0_out[0], and_9_out, and_10_out, and_11_out, and_12_out);
  Decoder #(.select(2), .enable("false")) decoder_1 (
    .out0(out_3), .out1(out_4), .out2(out_5), .out3(out_6), .sel(cin0_out));

  assign out_2 = 1'b0;

  // Notes on the sheet:
  //   ~S1
  //   ~S0
  //   S1
  //   S0
  //   S1
  //   S0
  //   S1
  //   ~S1
  //   S0
  //   ~S0
  //   cin1
endmodule
