// Logisim project swap.circ as structural Verilog
module swap (
  input  I1,
  input  I2,
  input  S,
  output T1,
  output T2
);

  wire and_1_out, and_2_out, and_3_out, and_4_out, not_1_out;

  not not_1 (not_1_out, S);
  and and_1 (and_1_out, I1, not_1_out);
  and and_2 (and_2_out, I2, S);
  and and_3 (and_3_out, I2, not_1_out);
  and and_4 (and_4_out, S, I1);
  or or_1 (T1, and_1_out, and_2_out);
  or or_2 (T2, and_3_out, and_4_out);
endmodule
